# Fritzing sketch Thermistor wiring (saved by Fritzing 0.9.3b)
breadboards: 1

parts:
  Part1 = Arduino Uno (Rev3) - ICSP
  R1 = Resistor [tolerance=±5% resistance=10k package="0402 [SMD]"]
  Thermistor = Temperature Sensor (Thermistor) [thermistor_type=NTC package=THT]

nets:
  N1: Part1.A0, R1.Pin_1, Thermistor.pin_1
  N2: Part1.5V, R1.Pin_0
  N3: Part1.GND, Thermistor.pin_0
